// Logisim project Chap3_1_基本RS触发器.circ as structural Verilog: 1 circuit, main circuit main
module main (
  input  R,
  input  S,
  output nQ,
  output Q
);

  nand nand_1 (nQ, R, Q);
  nand nand_2 (Q, nQ, S);

  // Notes on the sheet:
  //   G1
  //   输入变量R,S
  //   基本R-S触发器（与非门）
  //   输出变量/Q,Q
  //   G2
endmodule
