// Logisim project Chap4_6_2位二进制乘法器.circ as structural Verilog: 1 circuit, main circuit main
module main (
  input  A1,
  input  B1,
  input  A0,
  input  B0,
  output M3,
  output M2,
  output M1,
  output M0
);

  wire and_1_out, and_3_out, and_4_out;

  LED led_1 (.in(M3));
  and and_1 (and_1_out, A1, B1);
  xor xor_1 (M2, and_1_out, M3);
  and and_2 (M3, and_4_out, and_3_out);
  and and_3 (and_3_out, A1, B0);
  LED led_2 (.in(M3));
  xor xor_2 (M1, and_3_out, and_4_out);
  and and_4 (and_4_out, B1, A0);
  and and_5 (M0, A0, B0);

  // Notes on the sheet:
  //   中间进位：C2=A1B0A0B1
  //   输入变量：A1B1,A0B0
  //   2位二进制乘法器电路
  //   输出变量：M3~M0
  //   中间进位：C1=A1B0A0B1
endmodule
