// Logisim project Chap6_2_异步X1-X2-X3检测器.circ as structural Verilog: 1 circuit, main circuit main
module main (
  input  \置1 ,
  input  \清除 ,
  output Z
);

  wire and_1_out, and_2_out, and_3_out, and_4_out, or_1_out, or_2_out, X1_out, X2_out, Y1_q, Y1_qn, Y2_q,
       Y2_qn;

  LED led_1 (.in(X2_out));
  Button X1 (.out(X1_out));
  Button X2 (.out(X2_out));
  LED led_2 (.in(X1_out));
  and and_1 (and_1_out, Y2_qn, X1_out);
  and and_2 (and_2_out, X2_out, Y1_q);
  and and_3 (and_3_out, X2_out, Y2_q);
  and and_4 (and_4_out, X1_out, Y1_q);
  LED led_3 (.in(or_1_out));
  or or_1 (or_1_out, and_1_out, and_2_out, and_3_out);
  LED led_4 (.in(or_2_out));
  or or_2 (or_2_out, and_3_out, and_4_out);
  D_Flip_Flop Y2 (.clk(or_1_out), .D(Y2_qn), .Q(Y2_q), .Qn(Y2_qn), .preset(\置1 ), .reset(\清除 ));  // open: en
  D_Flip_Flop Y1 (.clk(or_2_out), .D(Y1_qn), .Q(Y1_q), .Qn(Y1_qn), .preset(\置1 ), .reset(\清除 ));  // open: en
  LED led_5 (.in(Y2_q));
  LED led_6 (.in(Y1_q));
  and and_5 (Z, Y2_q, Y1_q);

  // Notes on the sheet:
  //   输入信号
  //   输入信号
  //   观察点
  //   异步时序逻辑电路的X1-X2-X2序列检测器
  //   观察点
  //   D触发器的清除、置1端是高电平有效
  //   观察点
  //   状态流程：00--（X1）--10
  //   10--（X2）--01
  //   01--（X2）--11
  //   输出信号
  //   11--（Z=1）
  //   仿真结果：00--（X1）--10--（X2）--01--（X2）--10 为什么？
endmodule
