// Logisim project U201714722_计瀚东_全加全减电路.circ as structural Verilog: 1 circuit, main circuit main
module main (
  input  \A_被加数_被减数 ,
  input  \B_加数_减数 ,
  input  \C_上一位的进位信息 ,
  input  \M_0表示加_表示减 ,
  output \F_本位结果 ,
  output \G_本位进位结果 
);

  wire nand_1_out, nand_2_out, nand_3_out, xor_1_out, xor_2_out;

  xor xor_1 (xor_1_out, \A_被加数_被减数 , \M_0表示加_表示减 );
  xor xor_2 (xor_2_out, \A_被加数_被减数 , \B_加数_减数 );
  nand nand_1 (nand_1_out, xor_1_out, \B_加数_减数 );
  nand nand_2 (nand_2_out, \C_上一位的进位信息 , xor_1_out);
  nand nand_3 (nand_3_out, \C_上一位的进位信息 , \B_加数_减数 );
  xor xor_3 (\F_本位结果 , xor_2_out, \C_上一位的进位信息 );
  nand nand_4 (\G_本位进位结果 , nand_1_out, nand_3_out);
endmodule
