// Logisim project chap3_4_T触发器.circ as structural Verilog: 1 circuit, main circuit main
module main (
  input  CP,
  input  T,
  output nQ,
  output Q
);

  wire G3_out, G4_out;

  nand G1 (nQ, G3_out, Q);
  nand G3 (G3_out, Q, T, CP);
  nand G2 (Q, nQ, G4_out);
  nand G4 (G4_out, CP, T, nQ);

  // Notes on the sheet:
  //   钟控T触发器
  //   T
  //   0
  //   1
  //   功能表
  //   Qn+1
  //   Q
  //   ~Q
  //   功能说明
  //   不变
  //   翻转
endmodule
