// Logisim project chap4_2_组合三位二进制数数值比较器.circ as structural Verilog: 1 circuit, main circuit main
module main (
  input  a3,
  input  b3,
  input  a2,
  input  b2,
  input  a1,
  input  b1,
  output F
);

  wire xor_1_out, xor_2_out, xor_3_out;

  LED \u_观察点  (.in(xor_1_out));
  xor xor_1 (xor_1_out, a3, b3);
  LED \u_观察点_2  (.in(xor_2_out));
  xor xor_2 (xor_2_out, a2, b2);
  LED \u_观察点_3  (.in(xor_3_out));
  xor xor_3 (xor_3_out, a1, b1);
  nor nor_1 (F, xor_1_out, xor_2_out, xor_3_out);

  // Notes on the sheet:
  //   输入信号：
  //   A = a3 a2 a1
  //   B = b3 b2 b1
  //   比较两个3位二进制数是否相等的数值比较器
  //   输出信号
endmodule
