// Logisim project test 74181.circ as structural Verilog: 1 circuit, main circuit main
module main (
  input  [3:0] S,
  input  [3:0] A,
  input  [3:0] B,
  input  M,
  input  Cn,
  input  in_6,
  input  in_7,
  output G,
  output Cn_4,
  output P,
  output A_B,
  output [3:0] F
);

  wire clock_1_out, n74181_1_p1, n74181_1_p15, not_1_out, undriven;
  wire [2:0] bitadder_1_out;
  wire [3:0] counter_1_q, n74181_1_p2, ram_1_data;

  BitAdder #(.width(4)) bitadder_1 (.in0(n74181_1_p2), .out(bitadder_1_out));
  Clock clock_1 (.out(clock_1_out));
  not not_1 (not_1_out, Cn);
  Counter #(.width(4), .max('hf)) counter_1 (
    .load(in_6), .count(in_7), .Q(counter_1_q), .clk(clock_1_out), .clr(undriven));  // open: D, carry
  LED led_1 (.in(clock_1_out));
  // _74181 74181_1: pin names not known; wires that end beside it: n74181_1_p1, n74181_1_p2, bitadder_1_out, B[3], A[3], B[2], A[2], B[1], A[1], B[0], A[0], M, not_1_out, G, n74181_1_p15, P, F[3], F[2], A_B, F[1], F[0]
  not not_2 (Cn_4, n74181_1_p15);
  Hex_Digit_Display hex_digit_display_1 (.value(counter_1_q));  // open: dp
  Hex_Digit_Display hex_digit_display_2 (.value(F));  // open: dp
  Register register_1 ();  // open: D, en, Q, clk, clr
  Multiplexer #(.enable("false")) multiplexer_1 ();  // open: in0, in1, out, sel
  RAM #(.addrWidth(4), .dataWidth(4)) ram_1 (.addr(counter_1_q), .data(ram_1_data), .sel(1'b1));  // open: clk, ld, clr
  Hex_Digit_Display hex_digit_display_3 (.value(ram_1_data));  // open: dp
endmodule
