// Logisim project 一位二进制全加器.circ as structural Verilog: 1 circuit, main circuit main
module main (
  input  A,
  input  B,
  input  C1,
  output S,
  output C0
);

  wire and_1_out, and_2_out, xor_1_out;

  xor xor_1 (xor_1_out, A, B);
  and and_1 (and_1_out, B, A);
  and and_2 (and_2_out, xor_1_out, C1);
  xor xor_2 (S, xor_1_out, C1);
  or or_1 (C0, and_2_out, and_1_out);
endmodule
