// Logisim project 串行进位四位二进制并行加法器.circ as structural Verilog: 1 circuit, main circuit main
module main (
  input  A0,
  input  A1,
  input  A2,
  input  A3,
  input  B0,
  input  B1,
  input  B2,
  input  B4,
  input  C0,
  output S0,
  output S0_2,
  output S0_3,
  output S3,
  output C4
);

  wire main_1_c0, main_2_c0, main_3_c0;

  \一位二进制全加器_main  main_1 (.A(A0), .B(B0), .C1(C0), .S(S0), .C0(main_1_c0));
  \一位二进制全加器_main  main_2 (.A(A1), .B(B1), .C1(main_1_c0), .S(S0_2), .C0(main_2_c0));
  \一位二进制全加器_main  main_3 (.A(A2), .B(B2), .C1(main_2_c0), .S(S0_3), .C0(main_3_c0));
  \一位二进制全加器_main  main_4 (.A(A3), .B(B4), .C1(main_3_c0), .S(S3), .C0(C4));
endmodule
