// Logisim project 先行进位的四位二进制并行加法器.circ as structural Verilog: 1 circuit, main circuit main
module main (
  input  A0,
  input  A1,
  input  A2,
  input  A3,
  input  B0,
  input  B1,
  input  B2,
  input  B3,
  input  C0,
  output S2,
  output S0,
  output S1,
  output S3,
  output C4
);

  wire and_2_out, and_4_out, and_5_out, and_7_out, and_8_out, and_9_out, and_11_out, and_12_out, and_13_out,
       and_14_out, M0, M1, M2, M3, or_2_out, or_4_out, or_7_out, P0, P1, P2, P3, xor_1_out, xor_3_out,
       xor_5_out, xor_7_out;

  xor xor_1 (xor_1_out, A0, B0);
  and and_1 (M0, A0, B0);
  or or_1 (P0, A0, B0);
  xor xor_2 (S0, xor_1_out, C0);
  xor xor_3 (xor_3_out, A1, B1);
  and and_2 (and_2_out, P0, C0);
  or or_2 (or_2_out, M0, and_2_out);
  and and_3 (M1, A1, B1);
  or or_3 (P1, A1, B1);
  xor xor_4 (S1, xor_3_out, or_2_out);
  and and_4 (and_4_out, P1, M0);
  and and_5 (and_5_out, P1, P0, C0);
  xor xor_5 (xor_5_out, A2, B2);
  or or_4 (or_4_out, M1, and_4_out, and_5_out);
  and and_6 (M2, A2, B2);
  or or_5 (P2, A2, B2);
  xor xor_6 (S2, xor_5_out, or_4_out);
  xor xor_7 (xor_7_out, A3, B3);
  and and_7 (and_7_out, P2, M1);
  and and_8 (and_8_out, P2, P1, M0);
  and and_9 (and_9_out, P2, P1, P0, C0);
  and and_10 (M3, A3, B3);
  or or_6 (P3, A3, B3);
  or or_7 (or_7_out, M2, and_7_out, and_8_out, and_9_out);
  xor xor_8 (S3, xor_7_out, or_7_out);
  and and_11 (and_11_out, P3, M2);
  and and_12 (and_12_out, P3, P2, M1);
  and and_13 (and_13_out, P3, P2, P1, M0);
  and and_14 (and_14_out, P3, P2, P1, P0, C0);
  or or_8 (C4, M3, and_11_out, and_12_out, and_13_out, and_14_out);
endmodule
