// Logisim project 先行进位的四位二进制并行加法器封装版.circ as structural Verilog: 1 circuit, main circuit main
module main (
  input  in_1,
  input  in_2,
  input  in_3,
  input  in_4,
  input  in_5,
  input  in_6,
  input  in_7,
  input  in_8,
  input  in_9,
  output out_10,
  output out_11,
  output out_12,
  output out_13,
  output out_14
);

  // 先行进位的四位二进制并行加法器_main main_1: pin names not known; wires that end beside it: out_10, in_1, in_3, out_11, in_5, out_12, in_7

  // Other names for the same wires on the sheet: A0 = in_7; A1 = in_5; A2 = in_3; A3 = in_1; B0 = in_8; B1 = in_6;
  //   B2 = in_4; B3 = in_2; C0 = in_9; C4 = out_10; S0 = out_14; S1 = out_13; S2 = out_12; S3 = out_11
endmodule
