// Logisim project 四位二进制可逆计数器.circ as structural Verilog: 1 circuit, main circuit main
module main (
  input  CLR,
  input  CPu,
  input  CPd,
  output QA,
  output QB,
  output QC,
  output QD
);

  wire and_1_out, and_2_out, and_3_out, and_4_out, and_5_out, and_6_out, DA_qn, DB_qn, DC_qn, DD_qn,
       or_1_out, or_2_out, or_3_out, or_4_out;

  or or_1 (or_1_out, and_1_out, and_2_out);
  and and_1 (and_1_out, QB, QC, QD, CPu);
  D_Flip_Flop #(.trigger("falling")) DA (
    .clk(or_1_out), .D(DA_qn), .Q(QA), .Qn(DA_qn), .reset(CLR));  // open: preset, en
  and and_2 (and_2_out, DB_qn, DC_qn, DD_qn, CPd);
  or or_2 (or_2_out, and_3_out, and_4_out);
  and and_3 (and_3_out, QC, QD, CPu);
  D_Flip_Flop #(.trigger("falling")) DB (
    .clk(or_2_out), .D(DB_qn), .Q(QB), .Qn(DB_qn), .reset(CLR));  // open: preset, en
  and and_4 (and_4_out, DC_qn, DD_qn, CPd);
  or or_3 (or_3_out, and_5_out, and_6_out);
  and and_5 (and_5_out, QD, CPu);
  D_Flip_Flop #(.trigger("falling")) DC (
    .clk(or_3_out), .D(DC_qn), .Q(QC), .Qn(DC_qn), .reset(CLR));  // open: preset, en
  and and_6 (and_6_out, DD_qn, CPd);
  or or_4 (or_4_out, CPu, CPd);
  D_Flip_Flop #(.trigger("falling")) DD (
    .clk(or_4_out), .D(DD_qn), .Q(QD), .Qn(DD_qn), .reset(CLR));  // open: preset, en
endmodule
