// Logisim project 四位二进制数转8421电路方案一.circ as structural Verilog: 1 circuit, main circuit main
module main (
  input  A4,
  input  A3,
  input  A2,
  input  A1,
  output C2,
  output C3,
  output C4,
  output C1,
  output S4,
  output S3,
  output S2,
  output S1
);

  wire and_1_out, and_2_out, and_4_out, and_5_out, and_6_out, and_7_out, not_1_out, not_2_out, not_3_out,
       not_4_out;

  and and_1 (and_1_out, A4, A3);
  or or_1 (C1, and_1_out, and_2_out);
  and and_2 (and_2_out, A3, A2);
  and and_3 (S4, A4, not_1_out, not_2_out);
  not not_1 (not_1_out, A3);
  not not_2 (not_2_out, A2);
  not not_3 (not_3_out, A4);
  or or_2 (S3, and_5_out, and_4_out);
  and and_4 (and_4_out, A3, A2);
  and and_5 (and_5_out, not_3_out, A3);
  and and_6 (and_6_out, A4, A3);
  or or_3 (S2, and_6_out, and_7_out);
  and and_7 (and_7_out, not_4_out, A2);
  not not_4 (not_4_out, A4);

  assign C2 = 1'b0;
  assign C3 = 1'b0;
  assign C4 = 1'b0;
  assign S1 = A1;
endmodule
