// Logisim project 四位二进制数转8421电路方案二.circ as structural Verilog: 1 circuit, main circuit main
module main (
  input  A4,
  input  A3,
  input  A2,
  input  A1,
  output C4,
  output C3,
  output C2,
  output C1,
  output S4,
  output S3,
  output S2,
  output S1
);

  wire and_1_out, or_1_out;

  \先行进位的四位二进制并行加法器_main  main_1 (
    .A0(A1), .A1(A2), .A2(A3), .A3(A4), .B0(1'b0), .B1(and_1_out), .B2(and_1_out), .B3(1'b0), .C0(1'b0),
    .S0(S1), .S1(S2), .S2(S3), .S3(S4), .C4(C1));
  or or_1 (or_1_out, A2, A3);
  and and_1 (and_1_out, or_1_out, A4);

  assign C2 = 1'b0;
  assign C3 = 1'b0;
  assign C4 = 1'b0;
endmodule
