// Logisim project 实验室门禁系统.circ as structural Verilog: 1 circuit, main circuit main
module main (
  input  CPu,
  input  CLR,
  input  CPd,
  output out_4,
  output out_5,
  output out_6,
  output out_7,
  output out_8,
  output out_9,
  output out_10,
  output out_11,
  output out_12,
  output out_13,
  output out_14,
  output out_15,
  output out_16,
  output out_17,
  output \报警 
);

  wire main_3_c1, main_3_c2, main_3_c3, main_3_c4, main_3_s1, main_3_s2, main_3_s3, main_3_s4, main_4_s1,
       main_4_s2, main_4_s3, main_4_s4;

  \_7段译码器_main  main_1 (
    .A4(main_3_c4), .A3(main_3_c3), .A2(main_3_c2), .A1(main_3_c1), .a(out_4), .b(out_5), .c(out_6),
    .d(out_7), .e(out_8), .f(out_9), .g(out_10));
  \_7段译码器_main  main_2 (
    .A4(main_3_s4), .A3(main_3_s3), .A2(main_3_s2), .A1(main_3_s1), .a(out_11), .b(out_12), .c(out_13),
    .d(out_14), .e(out_15), .f(out_16), .g(out_17));
  \四位二进制数转8421电路方案二_main  main_3 (
    .C4(main_3_c4), .C3(main_3_c3), .C2(main_3_c2), .C1(main_3_c1), .S4(main_3_s4), .S3(main_3_s3),
    .S2(main_3_s2), .S1(main_3_s1), .A4(main_4_s4), .A3(main_4_s3), .A2(main_4_s2), .A1(main_4_s1));
  \实验室门禁计数器_main  main_4 (
    .CPu(CPu), .CLR(CLR), .CPd(CPd), .alarm(\报警 ), .S4(main_4_s4), .S3(main_4_s3), .S2(main_4_s2),
    .S1(main_4_s1));
endmodule
