// Logisim project 实验室门禁计数器.circ as structural Verilog: 1 circuit, main circuit main
module main (
  input  CPu,
  input  CLR,
  input  CPd,
  output alarm,
  output S4,
  output S3,
  output S2,
  output S1
);

  wire and_1_out, and_2_out, and_3_out, and_4_out, and_5_out, nor_1_out, not_1_out, not_2_out;

  or or_1 (alarm, and_1_out, and_2_out);
  and and_1 (and_1_out, CPd, nor_1_out);
  and and_2 (and_2_out, CPu, and_5_out);
  nor nor_1 (nor_1_out, S4, S3, S2, S1);
  not not_1 (not_1_out, and_5_out);
  and and_3 (and_3_out, not_1_out, CPu);
  and and_4 (and_4_out, CPd, not_2_out);
  not not_2 (not_2_out, nor_1_out);
  and and_5 (and_5_out, S4, S3, S2, S1);
  \四位二进制可逆计数器_main  main_1 (.CLR(CLR), .CPu(and_3_out), .CPd(and_4_out), .QA(S4), .QB(S3), .QC(S2), .QD(S1));
endmodule
