// Logisim project 最终实验室门禁系统.circ as structural Verilog: 1 circuit, main circuit main
module main (
  input  CPu,
  input  CLR,
  input  CPd
);

  wire main_1_out_4, main_1_out_5, main_1_out_6, main_1_out_7, main_1_out_8, main_1_out_9, main_1_out_10,
       main_1_out_11, main_1_out_12, main_1_out_13, main_1_out_14, main_1_out_15, main_1_out_16,
       main_1_out_17, \main_1_报警 ;

  _7_Segment_Display u_7_segment_display_1 (
    .g(main_1_out_10), .f(main_1_out_9), .a(main_1_out_4), .b(main_1_out_5), .e(main_1_out_8),
    .d(main_1_out_7), .c(main_1_out_6), .dp(1'b0));
  _7_Segment_Display u_7_segment_display_2 (
    .g(main_1_out_17), .f(main_1_out_16), .a(main_1_out_11), .b(main_1_out_12), .e(main_1_out_15),
    .d(main_1_out_14), .c(main_1_out_13), .dp(1'b0));
  \实验室门禁系统_main  main_1 (
    .CPu(CPu), .CLR(CLR), .CPd(CPd), .\报警 (\main_1_报警 ), .out_4(main_1_out_4), .out_5(main_1_out_5),
    .out_6(main_1_out_6), .out_7(main_1_out_7), .out_8(main_1_out_8), .out_9(main_1_out_9),
    .out_10(main_1_out_10), .out_11(main_1_out_11), .out_12(main_1_out_12), .out_13(main_1_out_13),
    .out_14(main_1_out_14), .out_15(main_1_out_15), .out_16(main_1_out_16), .out_17(main_1_out_17));
  LED led_1 (.in(\main_1_报警 ));
endmodule
