// Logisim project 测试电路-7段译码器.circ as structural Verilog: 1 circuit, main circuit main
module main (
  input  in_1,
  input  in_2,
  input  in_3,
  input  in_4
);

  wire main_1_a, main_1_b, main_1_c, main_1_d, main_1_e, main_1_f, main_1_g;

  \_7段译码器_main  main_1 (
    .A4(in_1), .A3(in_2), .A2(in_3), .A1(in_4), .a(main_1_a), .b(main_1_b), .c(main_1_c), .d(main_1_d),
    .e(main_1_e), .f(main_1_f), .g(main_1_g));
  _7_Segment_Display u_7_segment_display_1 (
    .g(main_1_g), .f(main_1_f), .a(main_1_a), .b(main_1_b), .e(main_1_e), .d(main_1_d), .c(main_1_c),
    .dp(1'b0));
endmodule
