// Logisim project 测试电路-四位二进制数转8421.circ as structural Verilog: 1 circuit, main circuit main
module main (
  input  in_1,
  input  in_2,
  input  in_3,
  input  in_4,
  input  in_5,
  input  in_6,
  input  in_7,
  input  in_8,
  input  in_9,
  input  in_10,
  input  in_11,
  input  in_12,
  input  in_13,
  input  in_14,
  output out_15,
  output out_16,
  output out_17,
  output out_18,
  output out_19,
  output out_20,
  output out_21,
  output out_22,
  output out_23,
  output out_24,
  output out_25,
  output out_26,
  output out_27,
  output out_28,
  output out_29,
  output out_30
);

  wire main_3_a, main_3_b, main_3_c, main_3_d, main_3_e, main_3_f, main_3_g, main_4_alarm;

  \四位二进制可逆计数器_main  main_1 (.CLR(in_2), .CPu(in_1), .CPd(in_3), .QA(out_15), .QB(out_16), .QC(out_17), .QD(out_18));
  \四位二进制数转8421电路方案二_main  main_2 (
    .C4(out_23), .C3(out_24), .C2(out_25), .C1(out_26), .S4(out_27), .S3(out_28), .S2(out_29), .S1(out_30),
    .A4(in_11), .A3(in_12), .A2(in_13), .A1(in_14));
  \_7段译码器_main  main_3 (
    .A4(in_4), .A3(in_5), .A2(in_6), .A1(in_7), .a(main_3_a), .b(main_3_b), .c(main_3_c), .d(main_3_d),
    .e(main_3_e), .f(main_3_f), .g(main_3_g));
  _7_Segment_Display u_7_segment_display_1 (
    .g(main_3_g), .f(main_3_f), .a(main_3_a), .b(main_3_b), .e(main_3_e), .d(main_3_d), .c(main_3_c),
    .dp(1'b0));
  \实验室门禁计数器_main  main_4 (
    .CPu(in_8), .CLR(in_9), .CPd(in_10), .alarm(main_4_alarm), .S4(out_19), .S3(out_20), .S2(out_21),
    .S1(out_22));
  LED led_1 (.in(main_4_alarm));
endmodule
